# Fritzing sketch Sprinklers (saved by Fritzing 0.9.3b)
circuit board: 8.46667cm x 5.64444cm
breadboards: 2

parts:
  U1 = ESP8266 WiFi Module [part_number=ESP8266]
  C1 = Ceramic Capacitor [capacitance=100nF package="100 mil [THT, multilayer]"]
  HLK-PM1 = HLK-PM01
  R1 = Resistor [tolerance=±5% resistance=10k package="0603 [SMD]"]
  R2 = Resistor [tolerance=±5% resistance=10k package="0603 [SMD]"]
  R3 = Resistor [tolerance=±5% resistance=10k package="0603 [SMD]"]
  R5 = Resistor [tolerance=±5% resistance=10k package="0603 [SMD]"]
  R6 = Resistor [tolerance=±5% resistance=10k package="0603 [SMD]"]
  R7 = Resistor [tolerance=±5% resistance=10k package="0603 [SMD]"]
  R8 = Resistor [tolerance=±5% resistance=10k package="0603 [SMD]"]
  R9 = Resistor [tolerance=±5% resistance=10k package="0603 [SMD]"]  # not connected
  LED1 = LED - 3mm [color="Red (633nm)" package="3 mm [THT]"]
  LED2 = LED - 3mm [color="Red (633nm)" package="3 mm [THT]"]
  LED3 = LED - 3mm [color="Red (633nm)" package="3 mm [THT]"]
  LED4 = LED - 3mm [color="Red (633nm)" package="3 mm [THT]"]
  LED5 = LED - 3mm [color="Red (633nm)" package="3 mm [THT]"]
  LED6 = LED - 3mm [color="Red (633nm)" package="3 mm [THT]"]
  LED7 = LED - 3mm [color="Red (633nm)" package="3 mm [THT]"]
  LED8 = LED - 3mm [color="Orange (620nm)" package="3 mm [THT]"]
  JP1 = Header 2 [package=molex-1x2_lock]
  JP2 = Header 3 [package=molex-1x3_lock]
  U3 = DIODE-ZENER [package=diode-zener]
  U4 = DIODE-ZENER [package=diode-zener]
  U5 = DIODE-ZENER [package=diode-zener]
  U6 = DIODE-ZENER [package=diode-zener]
  U7 = DIODE-ZENER [package=diode-zener]
  U8 = DIODE-ZENER [package=diode-zener]
  U9 = DIODE-ZENER [package=diode-zener]
  C2 = Capacitor Polarized [package=cpol-radial-10uf-25v]
  U10 = V_REG_LD1117VXX [package=78xxl]
  JP3 = Header 2 [package=molex-1x2_lock]
  R10 = Resistor [tolerance=±5% resistance=10k package="0603 [SMD]"]
  R11 = Resistor [tolerance=±5% resistance=10k package="0603 [SMD]"]
  R12 = Resistor [tolerance=±5% resistance=10k package="0603 [SMD]"]
  R13 = Resistor [tolerance=±5% resistance=10k package="0603 [SMD]"]

nets:
  N1: U1.RXD, JP1.1
  N2: U1.VCC, JP2.1, C2.+, U10.OUT, JP3.2, R10.Pin_0, R11.Pin_0
  N3: U1.GPIO_0, R12.Pin_0
  N4: U1.GPIO_2, R6.Pin_1
  N5: U1.CH_PD, R11.Pin_1
  GND: U1.GND, C1.0, HLK-PM1.-Vo, LED1.anode, LED2.anode, LED3.anode, LED4.anode, LED5.anode, LED6.anode, LED7.anode, LED8.anode, JP2.3, C2.-, U10.GND, JP3.1, R13.Pin_0
  N6: U1.TXD, JP1.2
  N7: U1.GPIO_15, R13.Pin_1
  N8: U1.GPIO_4, R7.Pin_1
  N9: U1.GPIO_5, R8.Pin_1
  N10: U1.GPIO_16, R3.Pin_1
  N11: U1.GPIO_14, R2.Pin_1
  N12: U1.GPIO_12, R1.Pin_1
  N13: U1.GPIO_13, R5.Pin_1
  N14: U1.REST, R10.Pin_1
  N15: C1.1, HLK-PM1.+Vo, U10.IN
  N16: R1.Pin_0, LED6.cathode
  N17: R2.Pin_0, LED7.cathode
  N18: R3.Pin_0, LED1.cathode
  N19: R5.Pin_0, LED5.cathode
  N20: R6.Pin_0, LED4.cathode
  N21: R7.Pin_0, LED3.cathode
  N22: R8.Pin_0, LED2.cathode
  N23: JP2.2, R12.Pin_1
  N24: U3.C, U4.C, U5.C, U6.C, U7.C, U8.C, U9.C
